# Fritzing sketch Air Quality Detector (saved by Fritzing 0.9.3b)
breadboards: 1

parts:
  Part1 = Photon
  U1 = LCD-16X2 [package=lcd-16x2]
  Part2 = Gas Sensor Breakout Board
  RHT1 = Humidity and Temperature Sensor RHT03
  U2 = POT [package=3362u]

nets:
  N1: Part1.A1, Part2.A1
  GND: Part1.GND, U1.VSS, U1.R_W, U1.K, Part2.GND, RHT1.GND_1, RHT1.GND_2, U2.E
  N2: Part1.D0, U1.DB7
  N3: Part1.D1, RHT1.Data-signal
  N4: Part1.D2, U1.DB6
  N5: Part1.D3, U1.DB5
  N6: Part1.D4, U1.DB4
  N7: Part1.D5, U1.E
  N8: Part1.D6, U1.RS
  3V3: Part1.3V3, U1.VDD, U1.A, Part2.B1, RHT1.Vcc, U2.A
  N9: U1.VO, U2.S

notes:
  fritzing does not include Dust sensor (part isn't available)
